# Fritzing sketch 001_BasicTempSensorLayout (saved by Fritzing 0.9.10b)
breadboards: 1

parts:
  DS1 = DS18B20 1-Wire Temperature Sensor [part_number=DS18B20]
  Raspberry_Pi_1 = Raspberry Pi 3 [part_number=RPI-3-V1.2]
  R1 = Resistor [tolerance=±5% resistance=4.7k package="2010 [SMD]"]

nets:
  GND: DS1.GND, Raspberry_Pi_1.GND
  N1: DS1.DQ, Raspberry_Pi_1.GPIO4, R1.Pin_0
  VDD: DS1.VDD, Raspberry_Pi_1.3v3, R1.Pin_1
